# Fritzing sketch arduinoscketch (saved by Fritzing 0.9.2b)

parts:
  Composant1 = Arduino Uno (Rev3)
  PIR1 = PIR sensor

nets:
  GND: Composant1.GND, PIR1.GND
  N1: Composant1.D2, PIR1.SIG
  5V: Composant1.5V, PIR1.VDD
