# Fritzing sketch nodearduino (saved by Fritzing 0.9.2b)
breadboards: 1

parts:
  R1 = Resistor [tolerance=±5% resistance=220 package=THT]
  Cellule_photoélectrique = Arduino Uno (Rev3)
  R2 = Photocell (LDR) [package=THT]

nets:
  N1: R1.Pin_1, Cellule_photoélectrique.GND
  N2: Cellule_photoélectrique.A0, R2.pin_1
  N3: Cellule_photoélectrique.5V, R2.pin_0
